# Fritzing sketch Semaforo (saved by Fritzing 0.9.3b)
breadboards: 1

parts:
  S1 = Pushbutton [package="[THT]"]
  S2 = Pushbutton [package="[THT]"]
  R1 = Resistor [tolerance=±5% resistance=220 package=THT]
  Componente1 = Arduino Uno (Rev3)
  R2 = Resistor [tolerance=±5% resistance=220 package=THT]
  R3 = Resistor [tolerance=±5% resistance=220 package=THT]
  R4 = Resistor [tolerance=±5% resistance=220 package=THT]
  R5 = Resistor [tolerance=±5% resistance=220 package=THT]
  LED1 = LED - 5mm [color="Red (633nm)" package="5 mm [THT]"]
  LED2 = LED - 5mm [color="Yellow (585nm)" package="5 mm [THT]"]
  LED3 = LED - 5mm [color="Green (555nm)" package="5 mm [THT]"]
  LED4 = LED - 5mm [color="Red (633nm)" package="5 mm [THT]"]
  LED5 = LED - 5mm [color="Yellow (585nm)" package="5 mm [THT]"]
  LED6 = LED - 5mm [color="Green (555nm)" package="5 mm [THT]"]
  R6 = Resistor [tolerance=±5% resistance=220 package=THT]
  R7 = Resistor [tolerance=±5% resistance=220 package=THT]
  R8 = Resistor [tolerance=±5% resistance=220 package=THT]

nets:
  N1: S1.Pin_1, S1.Pin_2, R1.Pin_0, Componente1.D2
  N2: S1.Pin_3, S1.Pin_4
  N3: S2.Pin_1, S2.Pin_2, Componente1.D3_PWM, R2.Pin_0
  N4: S2.Pin_3, S2.Pin_4, Componente1.5V
  N5: R1.Pin_1, Componente1.GND, R2.Pin_1, R3.Pin_1, R4.Pin_1, R5.Pin_1, R6.Pin_0, R7.Pin_0, R8.Pin_0
  N6: Componente1.D8, LED5.anode
  N7: Componente1.D9_PWM, LED6.anode
  N8: Componente1.D4, LED1.anode
  N9: Componente1.D5_PWM, LED2.anode
  N10: Componente1.D6_PWM, LED3.anode
  N11: Componente1.D7, LED4.anode
  N12: R3.Pin_0, LED1.cathode
  N13: R4.Pin_0, LED2.cathode
  N14: R5.Pin_0, LED3.cathode
  N15: LED4.cathode, R6.Pin_1
  N16: LED5.cathode, R7.Pin_1
  N17: LED6.cathode, R8.Pin_1
