# Fritzing sketch Dado (saved by Fritzing 0.9.3b)
breadboards: 1

parts:
  S1 = Pushbutton [package="[THT]"]
  R1 = Resistor [tolerance=±5% resistance=220 package=THT]
  Componente1 = Arduino Uno (Rev3)
  R3 = Resistor [tolerance=±5% resistance=220 package=THT]
  R4 = Resistor [tolerance=±5% resistance=220 package=THT]
  R5 = Resistor [tolerance=±5% resistance=220 package=THT]
  LED1 = LED - 5mm [color="Green (555nm)" package="5 mm [THT]"]
  LED2 = LED - 5mm [color="Green (555nm)" package="5 mm [THT]"]
  LED3 = LED - 5mm [color="Green (555nm)" package="5 mm [THT]"]
  LED4 = LED - 5mm [color="Green (555nm)" package="5 mm [THT]"]
  LED5 = LED - 5mm [color="Green (555nm)" package="5 mm [THT]"]
  LED6 = LED - 5mm [color="Green (555nm)" package="5 mm [THT]"]
  R6 = Resistor [tolerance=±5% resistance=220 package=THT]
  R7 = Resistor [tolerance=±5% resistance=220 package=THT]
  R8 = Resistor [tolerance=±5% resistance=220 package=THT]
  R9 = Resistor [tolerance=±5% resistance=220 package=THT]
  LED7 = LED - 5mm [color="Green (555nm)" package="5 mm [THT]"]

nets:
  N1: S1.Pin_1, S1.Pin_2, R1.Pin_0, Componente1.D3_PWM
  N2: S1.Pin_3, S1.Pin_4, Componente1.5V
  N3: R1.Pin_1, Componente1.GND, R3.Pin_1, R4.Pin_1, R5.Pin_1, R6.Pin_0, R7.Pin_0, R8.Pin_0, R9.Pin_1
  N4: Componente1.D8, LED4.anode
  N5: Componente1.D9_PWM, LED7.anode
  N6: Componente1.D10_PWM/SS, LED6.anode
  N7: Componente1.D4, LED5.cathode
  N8: Componente1.D5_PWM, LED1.anode
  N9: Componente1.D6_PWM, LED2.anode
  N10: Componente1.D7, LED3.anode
  N11: R3.Pin_0, LED1.cathode
  N12: R4.Pin_0, LED2.cathode
  N13: R5.Pin_0, LED3.cathode
  N14: LED4.cathode, R6.Pin_1
  N15: LED5.anode, R9.Pin_0
  N16: LED6.cathode, R8.Pin_1
  N17: R7.Pin_1, LED7.cathode
