# Fritzing sketch reproductorMusica (saved by Fritzing 0.9.3b)
breadboards: 1

parts:
  S1 = Pushbutton [package="[THT]"]
  Componente1 = Arduino Uno (Rev3)
  R1 = Resistor [tolerance=±5% resistance=220 package=THT]
  J1 = Piezo Speaker

nets:
  N1: S1.Pin_1, S1.Pin_2, Componente1.D3_PWM, R1.Pin_1
  N2: S1.Pin_3, S1.Pin_4, Componente1.5V
  N3: Componente1.D8, J1.pin1
  N4: Componente1.GND, R1.Pin_0
